# Fritzing sketch julie2 (saved by Fritzing 0.8.3b)
circuit board: 4.74279cm x 2.83744cm
breadboards: 1

parts:
  08M2 = PICAXE-08M [package=THT]
  R1 = Resistor [tolerance=±5% resistance=220 package=THT]
  R2 = Resistor [tolerance=±5% resistance=220 package=THT]
  R3 = Resistor [tolerance=±5% resistance=220 package=THT]
  J1 = female pin header, 2 pins [form="♀ (female)"]
  J2 = female pin header, 2 pins [form="♀ (female)"]
  J3 = female pin header, 2 pins [form="♀ (female)"]
  J4 = female pin header, 2 pins [form="♀ (female)"]
  R5 = Resistor [tolerance=±5% resistance=220 package=THT]
  J5 = female pin header, 2 pins [form="♀ (female)"]
  R6 = Resistor [tolerance=±5% resistance=220 package=THT]
  J6 = female pin header, 2 pins [form="♀ (female)"]
  J7 = female pin header, 2 pins [form="♀ (female)"]
  R4 = Resistor [tolerance=±5% resistance=220 package=THT]

nets:
  N1: 08M2.+V, J1.pin2, J2.pin2, J7.pin1
  N2: 08M2.Serial_In, R1.Pin_1
  N3: 08M2.In/Out_4_/_ADC_4, R2.Pin_1, R3.Pin_1
  N4: 08M2.In_3_/_Infrain, J1.pin1, R4.Pin_1
  N5: 08M2.In/Out_2_/_ADC_2_/_PWM_2, J5.pin2
  N6: 08M2.In/Out_1_/_ADC_1, J2.pin1, R5.Pin_0
  N7: 08M2.Serial_Out_/_Out_0_/_Infraout, R6.Pin_0
  N8: 08M2.0V, R1.Pin_0, J3.pin2, J4.pin2, R5.Pin_1, J5.pin1, J6.pin1, J7.pin2, R4.Pin_0
  N9: R2.Pin_0, J4.pin1
  N10: R3.Pin_0, J3.pin1
  N11: R6.Pin_1, J6.pin2
