# Fritzing sketch julie3 (saved by Fritzing 0.8.3b)
circuit board: 6.18063cm x 4.60022cm
breadboards: 1

parts:
  IC1 = PICAXE-08M [package=THT]
  LED2 = LED - 5mm [color="Red (633nm)" package="5 mm [THT]"]
  R1 = Resistor [tolerance=±5% resistance=220 package=THT]
  R2 = Resistor [tolerance=±5% resistance=220 package=THT]
  LED3 = LED - 5mm [color="Red (633nm)" package="5 mm [THT]"]
  S1 = Pushbutton [package="[THT]"]
  R3 = Resistor [tolerance=±5% resistance=10k package=THT]
  J1 = Piezo Speaker
  R5 = Resistor [tolerance=±5% resistance=10k package=THT]
  R6 = Resistor [tolerance=±5% resistance=220 package=THT]
  LED4 = LED - 5mm [color="Green (565nm)" package="5 mm [THT]"]
  Power_plug1 = Power plug
  R7 = Photocell (LDR) [package=THT]
  R8 = Resistor [tolerance=±5% resistance=10k package=THT]

nets:
  5V: IC1.+V, S1.Pin_1, S1.Pin_2, Power_plug1.GND, R7.pin_1
  N1: IC1.Serial_In, R8.Pin_0
  N2: IC1.In/Out_4_/_ADC_4, R1.Pin_0, R2.Pin_1
  N3: IC1.In_3_/_Infrain, S1.Pin_3, S1.Pin_4, R3.Pin_0
  N4: IC1.In/Out_2_/_ADC_2_/_PWM_2, J1.pin2
  N5: IC1.In/Out_1_/_ADC_1, R5.Pin_1, R7.pin_0
  N6: IC1.Serial_Out_/_Out_0_/_Infraout, R6.Pin_1
  GND: IC1.0V, LED2.cathode, LED3.cathode, R3.Pin_1, J1.pin1, R5.Pin_0, LED4.cathode, Power_plug1.VCC, R8.Pin_1
  N7: LED2.anode, R2.Pin_0
  N8: R1.Pin_1, LED3.anode
  N9: R6.Pin_0, LED4.anode
